// Logisim project Processeur.circ as structural Verilog: 34 circuits, main circuit Equal_8Bit
module main (
  input  [2:0] SlctA,
  input  [7:0] C,
  input  [2:0] SlctC,
  input  WE,
  input  [3:0] SlctOP,
  input  [2:0] SlctB,
  output [7:0] out_7,
  output [7:0] S,
  output Er,
  output [7:0] out_10
);

  wire clock_1_out;
  wire [7:0] bancreg_1_r1, bancreg_1_r2, bancreg_1_r3, bancreg_1_r4, bancreg_1_r5, bancreg_1_r6,
       bancreg_1_r7, bancreg_1_r8;

  Clock clock_1 (.out(clock_1_out));
  Multiplexer #(.select(3), .width(8)) multiplexer_1 (
    .in0(bancreg_1_r1), .in1(bancreg_1_r2), .in2(bancreg_1_r3), .in3(bancreg_1_r4), .in4(bancreg_1_r5),
    .in5(bancreg_1_r6), .in6(bancreg_1_r7), .in7(bancreg_1_r8), .out(out_7), .sel(SlctA));
  BancReg bancreg_1 (
    .CLK(clock_1_out), .C(C), .SlctC(SlctC), .WE(WE), .R1(bancreg_1_r1), .R2(bancreg_1_r2),
    .R3(bancreg_1_r3), .R4(bancreg_1_r4), .R5(bancreg_1_r5), .R6(bancreg_1_r6), .R7(bancreg_1_r7),
    .R8(bancreg_1_r8));
  Multiplexer #(.select(3), .width(8)) multiplexer_2 (
    .in0(bancreg_1_r1), .in1(bancreg_1_r2), .in2(bancreg_1_r3), .in3(bancreg_1_r4), .in4(bancreg_1_r5),
    .in5(bancreg_1_r6), .in6(bancreg_1_r7), .in7(bancreg_1_r8), .out(out_10), .sel(SlctB));
  ALU alu_1 (.A(out_7), .B(out_10), .slctOP(SlctOP), .S(S), .Er(Er));
endmodule

module BancReg (
  input  CLK,
  input  [7:0] C,
  input  [2:0] SlctC,
  input  WE,
  output [7:0] R1,
  output [7:0] R2,
  output [7:0] R3,
  output [7:0] R4,
  output [7:0] R5,
  output [7:0] R6,
  output [7:0] R7,
  output [7:0] R8
);

  wire decoder_1_out0, decoder_1_out1, decoder_1_out2, decoder_1_out3, decoder_1_out4, decoder_1_out5,
       decoder_1_out6, decoder_1_out7;

  Decoder #(.select(3)) decoder_1 (
    .out0(decoder_1_out0), .out1(decoder_1_out1), .out2(decoder_1_out2), .out3(decoder_1_out3),
    .out4(decoder_1_out4), .out5(decoder_1_out5), .out6(decoder_1_out6), .out7(decoder_1_out7), .sel(SlctC),
    .en(WE));
  // NoConnect on C[7:1]
  Reg_8Bit reg_8bit_1 (.D(C), .WE(decoder_1_out0), .CLK(CLK), .Q(R1));
  Reg_8Bit reg_8bit_2 (.D(C), .WE(decoder_1_out1), .CLK(CLK), .Q(R2));
  Reg_8Bit reg_8bit_3 (.D(C), .WE(decoder_1_out2), .CLK(CLK), .Q(R3));
  Reg_8Bit reg_8bit_4 (.D(C), .WE(decoder_1_out3), .CLK(CLK), .Q(R4));
  Reg_8Bit reg_8bit_5 (.D(C), .WE(decoder_1_out4), .CLK(CLK), .Q(R5));
  Reg_8Bit reg_8bit_6 (.D(C), .WE(decoder_1_out5), .CLK(CLK), .Q(R6));
  Reg_8Bit reg_8bit_7 (.D(C), .WE(decoder_1_out6), .CLK(CLK), .Q(R7));
  Reg_1Bit reg_1bit_1 (.D(C[0]), .WE(decoder_1_out7), .CLK(CLK), .Q(R8[0]));

  assign R8[7:1] = {7{1'b0}};
endmodule

module Reg_8Bit (
  input  [7:0] D,
  input  WE,
  input  CLK,
  output [7:0] Q
);

  wire and_1_out;

  and and_1 (and_1_out, WE, CLK);
  D_Flip_Flop d_ff_1 (.D(D[0]), .clk(and_1_out), .Q(Q[0]));  // open: Qn, preset, reset
  D_Flip_Flop d_ff_2 (.D(D[1]), .clk(and_1_out), .Q(Q[1]));  // open: Qn, preset, reset
  D_Flip_Flop d_ff_3 (.D(D[2]), .clk(and_1_out), .Q(Q[2]));  // open: Qn, preset, reset
  D_Flip_Flop d_ff_4 (.D(D[3]), .clk(and_1_out), .Q(Q[3]));  // open: Qn, preset, reset
  D_Flip_Flop d_ff_5 (.D(D[4]), .clk(and_1_out), .Q(Q[4]));  // open: Qn, preset, reset
  D_Flip_Flop d_ff_6 (.D(D[5]), .clk(and_1_out), .Q(Q[5]));  // open: Qn, preset, reset
  D_Flip_Flop d_ff_7 (.D(D[6]), .clk(and_1_out), .Q(Q[6]));  // open: Qn, preset, reset
  D_Flip_Flop d_ff_8 (.D(D[7]), .clk(and_1_out), .Q(Q[7]));  // open: Qn, preset, reset
endmodule

module Reg_1Bit (
  input  D,
  input  WE,
  input  CLK,
  output Q
);

  wire and_1_out;

  and and_1 (and_1_out, WE, CLK);
  D_Flip_Flop d_ff_1 (.D(D), .clk(and_1_out), .Q(Q));  // open: Qn, preset, reset
endmodule

module ALU (
  input  [7:0] A,
  input  [7:0] B,
  input  [3:0] slctOP,
  output [7:0] S,
  output Er
);

  wire bloc_op_ari_1_err;
  wire [7:0] bloc_op_ari_1_s, bloc_op_comp_1_s, bloc_op_log_1_s, bloc_op_rot_1_s;

  BLOC_OP_LOG bloc_op_log_1 (.SlctOP(slctOP[3:2]), .A(A), .B(B), .S(bloc_op_log_1_s));
  BLOC_OP_COMP bloc_op_comp_1 (.A(A), .SlctOP(slctOP[3:2]), .B(B), .S(bloc_op_comp_1_s));
  BLOC_OP_ROT bloc_op_rot_1 (.A(A), .SlctOP(slctOP[3:2]), .S(bloc_op_rot_1_s));
  BLOC_OP_ARI bloc_op_ari_1 (.A(A), .SlctOP(slctOP[3:2]), .B(B), .S(bloc_op_ari_1_s), .Err(bloc_op_ari_1_err));
  Multiplexer #(.select(2), .width(8)) multiplexer_1 (
    .in0(bloc_op_log_1_s), .in1(bloc_op_comp_1_s), .in2(bloc_op_rot_1_s), .in3(bloc_op_ari_1_s), .out(S),
    .sel(slctOP[1:0]));
  Multiplexer #(.select(2)) multiplexer_2 (
    .in0(1'b0), .in1(1'b0), .in2(1'b0), .in3(bloc_op_ari_1_err), .out(Er), .sel(slctOP[1:0]));
endmodule

module BLOC_OP_LOG (
  input  [1:0] SlctOP,
  input  [7:0] A,
  input  [7:0] B,
  output [7:0] S
);

  wire [7:0] and_8bit_1_s, or_8bit_1_s, xor_8bit_1_s;

  And_8Bit and_8bit_1 (.A(A), .B(B), .S(and_8bit_1_s));
  Or_8Bit or_8bit_1 (.A(A), .B(B), .S(or_8bit_1_s));
  Xor_8Bit xor_8bit_1 (.A(A), .B(B), .S(xor_8bit_1_s));
  Multiplexer #(.select(2), .width(8)) multiplexer_1 (
    .in0(and_8bit_1_s), .in1(and_8bit_1_s), .in2(or_8bit_1_s), .in3(xor_8bit_1_s), .out(S), .sel(SlctOP));
endmodule

module BLOC_OP_COMP (
  input  [7:0] A,
  input  [1:0] SlctOP,
  input  [7:0] B,
  output [7:0] S
);

  wire diff_8bit_1_s, equal_8bit_1_s, inf_8bit_1_s, sup_8bit_1_s;

  Equal_8Bit equal_8bit_1 (.A(A), .B(B), .S(equal_8bit_1_s));
  Diff_8Bit diff_8bit_1 (.A(A), .B(B), .S(diff_8bit_1_s));
  Inf_8Bit inf_8bit_1 (.A(A), .B(B), .S(inf_8bit_1_s));
  Sup_8Bit sup_8bit_1 (.A(A), .B(B), .S(sup_8bit_1_s));
  Multiplexer #(.select(2)) multiplexer_1 (
    .in0(equal_8bit_1_s), .in1(diff_8bit_1_s), .in2(inf_8bit_1_s), .in3(sup_8bit_1_s), .out(S[0]),
    .sel(SlctOP));

  assign S[7:1] = {7{1'b0}};
endmodule

module BLOC_OP_ARI (
  input  [7:0] A,
  input  [1:0] SlctOP,
  input  [7:0] B,
  output [7:0] S,
  output Err
);

  wire add_8bit_1_er, sub_8bit_1_er;
  wire [7:0] add_8bit_1_s, sub_8bit_1_s;

  Add_8Bit add_8bit_1 (.A(A), .B(B), .S(add_8bit_1_s), .Er(add_8bit_1_er));
  Sub_8Bit sub_8bit_1 (.A(A), .B(B), .S(sub_8bit_1_s), .Er(sub_8bit_1_er));
  or or_1 (Err, add_8bit_1_er, sub_8bit_1_er);
  Multiplexer #(.width(8)) multiplexer_1 (.in0(add_8bit_1_s), .in1(sub_8bit_1_s), .out(S), .sel(SlctOP[1]));
endmodule

module BLOC_OP_ROT (
  input  [7:0] A,
  input  [1:0] SlctOP,
  output [7:0] S
);

  wire [7:0] asr_8bit_1_s, lsl_8bit_1_s, lsr_8bit_1_s, rol_8bit_1_s;

  Lsl_8Bit lsl_8bit_1 (.A(A), .S(lsl_8bit_1_s));
  Lsr_8Bit lsr_8bit_1 (.A(A), .S(lsr_8bit_1_s));
  Asr_8Bit asr_8bit_1 (.A(A), .S(asr_8bit_1_s));
  Rol_8Bit rol_8bit_1 (.A(A), .S(rol_8bit_1_s));
  Multiplexer #(.select(2), .width(8)) multiplexer_1 (
    .in0(lsl_8bit_1_s), .in1(lsr_8bit_1_s), .in2(asr_8bit_1_s), .in3(rol_8bit_1_s), .out(S), .sel(SlctOP));
endmodule

module Equal_1Bit (
  input  A,
  input  B,
  output S
);

  wire and_1_out, and_2_out, not_1_out, not_2_out;

  and and_1 (and_1_out, A, B);
  not not_1 (not_1_out, A);
  and and_2 (and_2_out, not_1_out, not_2_out);
  not not_2 (not_2_out, B);
  or or_1 (S, and_1_out, and_2_out);
endmodule

module Diff_1Bit (
  input  A,
  input  B,
  output S
);

  wire and_1_out, and_2_out, not_1_out, not_2_out, or_1_out;

  and and_1 (and_1_out, A, B);
  not not_1 (not_1_out, A);
  and and_2 (and_2_out, not_1_out, not_2_out);
  not not_2 (not_2_out, B);
  or or_1 (or_1_out, and_1_out, and_2_out);
  not not_3 (S, or_1_out);
endmodule

module Inf_1Bit (
  input  A,
  input  B,
  output S
);

  wire not_1_out;

  not not_1 (not_1_out, A);
  and and_1 (S, not_1_out, B);
endmodule

module InfFull_1Bit (
  input  A,
  input  B,
  input  R_1,
  output S
);

  wire and_1_out, and_2_out, and_3_out, not_1_out;

  not not_1 (not_1_out, A);
  and and_1 (and_1_out, not_1_out, R_1);
  and and_2 (and_2_out, not_1_out, B);
  and and_3 (and_3_out, B, R_1);
  or or_1 (S, and_1_out, and_2_out, and_3_out);
endmodule

module Sup_1Bit (
  input  A,
  input  B,
  output S
);

  wire not_1_out;

  not not_1 (not_1_out, A);
  and and_1 (S, not_1_out, B);
endmodule

module SupFull_1Bit (
  input  A,
  input  B,
  input  R_1,
  output S
);

  wire and_1_out, and_2_out, and_3_out, not_1_out;

  not not_1 (not_1_out, B);
  and and_1 (and_1_out, A, R_1);
  and and_2 (and_2_out, A, not_1_out);
  and and_3 (and_3_out, not_1_out, R_1);
  or or_1 (S, and_1_out, and_2_out, and_3_out);
endmodule

module Equal_8Bit (
  input  [7:0] A,
  input  [7:0] B,
  output S
);

  wire equal_1bit_1_s, equal_1bit_2_s, equal_1bit_3_s, equal_1bit_4_s, equal_1bit_5_s, equal_1bit_6_s,
       equal_1bit_7_s, equal_1bit_8_s;

  Equal_1Bit equal_1bit_1 (.A(A[0]), .B(B[0]), .S(equal_1bit_1_s));
  Equal_1Bit equal_1bit_2 (.A(A[1]), .B(B[1]), .S(equal_1bit_2_s));
  Equal_1Bit equal_1bit_3 (.A(A[2]), .B(B[2]), .S(equal_1bit_3_s));
  Equal_1Bit equal_1bit_4 (.A(A[3]), .B(B[3]), .S(equal_1bit_4_s));
  Equal_1Bit equal_1bit_5 (.A(A[4]), .B(B[4]), .S(equal_1bit_5_s));
  Equal_1Bit equal_1bit_6 (.A(A[5]), .B(B[5]), .S(equal_1bit_6_s));
  Equal_1Bit equal_1bit_7 (.A(A[6]), .B(B[6]), .S(equal_1bit_7_s));
  Equal_1Bit equal_1bit_8 (.A(A[7]), .B(B[7]), .S(equal_1bit_8_s));
  and and_1 (S, equal_1bit_1_s, equal_1bit_2_s, equal_1bit_3_s, equal_1bit_4_s, equal_1bit_5_s, equal_1bit_6_s, equal_1bit_7_s, equal_1bit_8_s);
endmodule

module Diff_8Bit (
  input  [7:0] A,
  input  [7:0] B,
  output S
);

  wire diff_1bit_1_s, diff_1bit_2_s, diff_1bit_3_s, diff_1bit_4_s, diff_1bit_5_s, diff_1bit_6_s,
       diff_1bit_7_s, diff_1bit_8_s;

  Diff_1Bit diff_1bit_1 (.A(A[0]), .B(B[0]), .S(diff_1bit_1_s));
  Diff_1Bit diff_1bit_2 (.A(A[1]), .B(B[1]), .S(diff_1bit_2_s));
  Diff_1Bit diff_1bit_3 (.A(A[2]), .B(B[2]), .S(diff_1bit_3_s));
  Diff_1Bit diff_1bit_4 (.A(A[3]), .B(B[3]), .S(diff_1bit_4_s));
  Diff_1Bit diff_1bit_5 (.A(A[4]), .B(B[4]), .S(diff_1bit_5_s));
  Diff_1Bit diff_1bit_6 (.A(A[5]), .B(B[5]), .S(diff_1bit_6_s));
  Diff_1Bit diff_1bit_7 (.A(A[6]), .B(B[6]), .S(diff_1bit_7_s));
  Diff_1Bit diff_1bit_8 (.A(A[7]), .B(B[7]), .S(diff_1bit_8_s));
  or or_1 (S, diff_1bit_1_s, diff_1bit_2_s, diff_1bit_3_s, diff_1bit_4_s, diff_1bit_5_s, diff_1bit_6_s, diff_1bit_7_s, diff_1bit_8_s);
endmodule

module Inf_8Bit (
  input  [7:0] A,
  input  [7:0] B,
  output S
);

  wire inffull_1bit_1_s, inffull_1bit_2_s, inffull_1bit_3_s, inffull_1bit_4_s, inffull_1bit_5_s,
       inffull_1bit_6_s, inffull_1bit_7_s;

  InfFull_1Bit inffull_1bit_1 (.A(A[0]), .B(B[0]), .R_1(1'b0), .S(inffull_1bit_1_s));
  InfFull_1Bit inffull_1bit_2 (.A(A[1]), .B(B[1]), .R_1(inffull_1bit_1_s), .S(inffull_1bit_2_s));
  InfFull_1Bit inffull_1bit_3 (.A(A[2]), .B(B[2]), .R_1(inffull_1bit_2_s), .S(inffull_1bit_3_s));
  InfFull_1Bit inffull_1bit_4 (.A(A[3]), .B(B[3]), .R_1(inffull_1bit_3_s), .S(inffull_1bit_4_s));
  InfFull_1Bit inffull_1bit_5 (.A(A[4]), .B(B[4]), .R_1(inffull_1bit_4_s), .S(inffull_1bit_5_s));
  InfFull_1Bit inffull_1bit_6 (.A(A[5]), .B(B[5]), .R_1(inffull_1bit_5_s), .S(inffull_1bit_6_s));
  InfFull_1Bit inffull_1bit_7 (.A(A[6]), .B(B[6]), .R_1(inffull_1bit_6_s), .S(inffull_1bit_7_s));
  InfFull_1Bit inffull_1bit_8 (.A(A[7]), .B(B[7]), .R_1(inffull_1bit_7_s), .S(S));
endmodule

module Sup_8Bit (
  input  [7:0] A,
  input  [7:0] B,
  output S
);

  wire supfull_1bit_1_s, supfull_1bit_2_s, supfull_1bit_3_s, supfull_1bit_4_s, supfull_1bit_5_s,
       supfull_1bit_6_s, supfull_1bit_7_s;

  SupFull_1Bit supfull_1bit_1 (.A(A[0]), .B(B[0]), .R_1(1'b0), .S(supfull_1bit_1_s));
  SupFull_1Bit supfull_1bit_2 (.A(A[1]), .B(B[1]), .R_1(supfull_1bit_1_s), .S(supfull_1bit_2_s));
  SupFull_1Bit supfull_1bit_3 (.A(A[2]), .B(B[2]), .R_1(supfull_1bit_2_s), .S(supfull_1bit_3_s));
  SupFull_1Bit supfull_1bit_4 (.A(A[3]), .B(B[3]), .R_1(supfull_1bit_3_s), .S(supfull_1bit_4_s));
  SupFull_1Bit supfull_1bit_5 (.A(A[4]), .B(B[4]), .R_1(supfull_1bit_4_s), .S(supfull_1bit_5_s));
  SupFull_1Bit supfull_1bit_6 (.A(A[5]), .B(B[5]), .R_1(supfull_1bit_5_s), .S(supfull_1bit_6_s));
  SupFull_1Bit supfull_1bit_7 (.A(A[6]), .B(B[6]), .R_1(supfull_1bit_6_s), .S(supfull_1bit_7_s));
  SupFull_1Bit supfull_1bit_8 (.A(A[7]), .B(B[7]), .R_1(supfull_1bit_7_s), .S(S));
endmodule

module And_8Bit (
  input  [7:0] A,
  input  [7:0] B,
  output [7:0] S
);

  assign S = A & B;  // AND_Gate and_1, 8 bits wide
endmodule

module Or_8Bit (
  input  [7:0] A,
  input  [7:0] B,
  output [7:0] S
);

  assign S = A | B;  // OR_Gate or_1, 8 bits wide
endmodule

module Xor_8Bit (
  input  [7:0] A,
  input  [7:0] B,
  output [7:0] S
);

  assign S = A ^ B;  // XOR_Gate xor_1, 8 bits wide
endmodule

module Lsl_8Bit (
  input  [7:0] A,
  output [7:0] S
);

  // NoConnect on A[7]

  assign S = {A[6:0], 1'b0};
endmodule

module Lsr_8Bit (
  input  [7:0] A,
  output [7:0] S
);

  // NoConnect on A[0]

  assign S = {1'b0, A[7:1]};
endmodule

module Asr_8Bit (
  input  [7:0] A,
  output [7:0] S
);

  // NoConnect on A[0]

  assign S = {{2{A[7]}}, A[6:1]};
endmodule

module Rol_8Bit (
  input  [7:0] A,
  output [7:0] S
);


  assign S = {A[6:0], A[7]};
endmodule

module Ror_8Bit (
  input  [7:0] A,
  output [7:0] S
);


  assign S = {A[0], A[7:1]};
endmodule

module Add_1Bit (
  input  Re,
  input  A,
  input  B,
  output S,
  output Rs
);

  wire and_1_out, and_2_out, or_1_out, xor_1_out;

  xor xor_1 (xor_1_out, A, B);
  or or_1 (or_1_out, B, Re);
  xor xor_2 (S, xor_1_out, Re);
  and and_1 (and_1_out, or_1_out, A);
  or or_2 (Rs, and_1_out, and_2_out);
  and and_2 (and_2_out, B, Re);
endmodule

module Add_8Bit (
  input  [7:0] A,
  input  [7:0] B,
  output [7:0] S,
  output Er
);

  wire add_1bit_1_rs, add_1bit_2_rs, add_1bit_3_rs, add_1bit_4_rs, add_1bit_5_rs, add_1bit_6_rs,
       add_1bit_7_rs;

  Add_1Bit add_1bit_1 (.Re(1'b0), .A(A[0]), .B(B[0]), .S(S[0]), .Rs(add_1bit_1_rs));
  Add_1Bit add_1bit_2 (.Re(add_1bit_1_rs), .A(A[1]), .B(B[1]), .S(S[1]), .Rs(add_1bit_2_rs));
  Add_1Bit add_1bit_3 (.Re(add_1bit_2_rs), .A(A[2]), .B(B[2]), .S(S[2]), .Rs(add_1bit_3_rs));
  Add_1Bit add_1bit_4 (.Re(add_1bit_3_rs), .A(A[3]), .B(B[3]), .S(S[3]), .Rs(add_1bit_4_rs));
  Add_1Bit add_1bit_5 (.Re(add_1bit_4_rs), .A(A[4]), .B(B[4]), .S(S[4]), .Rs(add_1bit_5_rs));
  Add_1Bit add_1bit_6 (.Re(add_1bit_5_rs), .A(A[5]), .B(B[5]), .S(S[5]), .Rs(add_1bit_6_rs));
  Add_1Bit add_1bit_7 (.Re(add_1bit_6_rs), .A(A[6]), .B(B[6]), .S(S[6]), .Rs(add_1bit_7_rs));
  Add_1Bit add_1bit_8 (.Re(add_1bit_7_rs), .A(A[7]), .B(B[7]), .S(S[7]), .Rs(Er));
endmodule

module CC2_8Bit (
  input  [7:0] A,
  output [7:0] S,
  output Er
);

  wire add_8bit_1_er;
  wire [7:0] not_1_out;

  assign not_1_out = ~A;  // NOT_Gate not_1, 8 bits wide
  Add_8Bit add_8bit_1 (.A(not_1_out), .B(8'h1), .S(S), .Er(add_8bit_1_er));
  // NoConnect on add_8bit_1_er
  Equal_8Bit equal_8bit_1 (.A(A), .B(8'h80), .S(Er));
endmodule

module Sub_8Bit (
  input  [7:0] A,
  input  [7:0] B,
  output [7:0] S,
  output Er
);

  wire add_8bit_1_er, cc2_8bit_1_er;
  wire [7:0] cc2_8bit_1_s;

  CC2_8Bit cc2_8bit_1 (.A(B), .S(cc2_8bit_1_s), .Er(cc2_8bit_1_er));
  Add_8Bit add_8bit_1 (.A(A), .B(cc2_8bit_1_s), .S(S), .Er(add_8bit_1_er));
  or or_1 (Er, add_8bit_1_er, cc2_8bit_1_er);
endmodule

module Decodeur (
  input  CLK,
  input  [23:0] in_2,
  output [2:0] OPP,
  output [1:0] Typ,
  output WE,
  output [2:0] Rin1,
  output [2:0] Rin2,
  output [3:0] Rout
);

  wire [23:0] reg_24bit_1_q;

  Reg_24Bit reg_24bit_1 (.CLK(CLK), .D(in_2), .Q(reg_24bit_1_q));  // open: WE
  Deco_TypOP deco_typop_1 (.E(reg_24bit_1_q[7:0]), .Op(OPP), .Typ(Typ));
endmodule

module Reg_24Bit (
  input  CLK,
  input  WE,
  input  [23:0] D,
  output [23:0] Q
);

  Reg_8Bit reg_8bit_1 (.D(D[7:0]), .WE(WE), .CLK(CLK), .Q(Q[7:0]));
  Reg_8Bit reg_8bit_2 (.D(D[15:8]), .WE(WE), .CLK(CLK), .Q(Q[15:8]));
  Reg_8Bit reg_8bit_3 (.D(D[23:16]), .WE(WE), .CLK(CLK), .Q(Q[23:16]));
endmodule

module Deco_TypOP (
  input  [7:0] E,
  output [2:0] Op,
  output [1:0] Typ
);


  assign Op = E[2:0];
  assign Typ = E[4:3];
endmodule
